# Fritzing sketch estacionamiento (saved by Fritzing 0.9.0b)
breadboards: 1

parts:
  S1 = Pushbutton [package=THT]
  S2 = Pushbutton [package=THT]
  C1 = Electrolytic Capacitor [capacitance=1µF voltage=10V package="100 mil [THT, electrolytic]"]
  Parte1 = Arduino Mega 2560 (Rev3)
  R2 = Resistor [tolerance=±5% resistance=10k package=THT]
  R3 = Resistor [tolerance=±5% resistance=10k package=THT]
  7_Segment2 = 7 Segment Display
  J1 = Basic Servo

nets:
  N1: S1.leg0, S2.leg0, C1.+, Parte1.5V
  N2: S1.leg1, Parte1.A1, R3.Pin_0
  N3: S2.leg1, Parte1.A0, R2.Pin_1
  N4: C1.-, Parte1.GND, R2.Pin_0, R3.Pin_1, 7_Segment2.common_cathode#3
  N5: Parte1.D9_PWM, J1.pulse
  N6: Parte1.D8_PWM, 7_Segment2.Segment_F
  N7: Parte1.D2_PWM, 7_Segment2.Segment_A#1
  N8: Parte1.D3_PWM, 7_Segment2.Segment_B
  N9: Parte1.D4_PWM, 7_Segment2.Segment_C
  N10: Parte1.D5_PWM, 7_Segment2.Segment_D
  N11: Parte1.D6_PWM, 7_Segment2.Segment_E
  N12: Parte1.D7_PWM, 7_Segment2.Segment_A#10
